# Fritzing sketch Untitled Sketch (saved by Fritzing 0.9.3b)

parts:
  U1 = NodeMCU V1.0
  part = Resistor [tolerance=±5% resistance=10k package=THT]
  part_2 = Resistor [tolerance=±2% resistance=100 package=THT]
  Q1 = Basic FET N-Channel [package="TO220 [THT]"]
  Power_plug1 = Power plug
  Power_plug2 = Power plug
  J1 = Screw terminal - 2 pins [package=THT]

nets:
  N1: U1.D1, part_2.Pin_1
  GND: U1.GND, part.Pin_1, Q1.source, Power_plug1.GND, Power_plug2.GND
  VIN: U1.Vin, Power_plug2.VCC
  N2: part_2.Pin_0, Q1.gate
  N3: Q1.drain, J1.pin1
  N4: Power_plug1.VCC, J1.pin2

notes:
  Лента
  12 Вольт
  5Вольт

custom parts:
  NodeMCU V1.0: ESP8266 based NodeMCU
