# Fritzing sketch Untitled Sketch 2 (saved by Fritzing 0.9.3b)
breadboards: 1

parts:
  S1 = Pushbutton [package="[THT]"]
  U1 = NodeMCU V1.0
  part = Resistor [tolerance=±5% resistance=10k package=THT]

nets:
  N1: S1.Pin_1, S1.Pin_2, U1.D1, part.Pin_0
  N2: S1.Pin_3, S1.Pin_4, U1.3V3, part.Pin_1

custom parts:
  NodeMCU V1.0: ESP8266 based NodeMCU
