# Fritzing sketch sheme (saved by Fritzing 0.9.3b)
breadboards: 1

parts:
  U1 = NodeMCU V1.0
  Q1 = Basic FET N-Channel [package="D2Pak [SMD]"]
  Q2 = Basic FET N-Channel [package="D2Pak [SMD]"]
  Q3 = Basic FET N-Channel [package="D2Pak [SMD]"]
  part = Resistor [tolerance=±5% resistance=100 package=THT]
  part_2 = Resistor [tolerance=±5% resistance=100 package=THT]
  part_3 = Resistor [tolerance=±5% resistance=100 package=THT]
  Power_plug1 = Power plug
  part_4 = Resistor [tolerance=±5% resistance=10k package=THT]
  part_5 = Resistor [tolerance=±5% resistance=10k package=THT]
  part_6 = Resistor [tolerance=±5% resistance=10k package=THT]

nets:
  N1: U1.D1, part.Pin_1
  N2: U1.D2, part_2.Pin_1
  N3: U1.D3, part_3.Pin_1
  GND: U1.GND, Q1.source, Q2.source, Q3.source, Power_plug1.GND, part_4.Pin_0, part_5.Pin_0
  N4: Q1.Gate, part.Pin_0, part_6.Pin_1
  N5: Q2.Gate, part_2.Pin_0, part_5.Pin_1
  N6: Q3.Gate, part_3.Pin_0, part_4.Pin_1

notes:
  Синий Зеленый Красный 12 Вольт
  12 Вольт

custom parts:
  NodeMCU V1.0: ESP8266 based NodeMCU
