# Fritzing sketch scheme (saved by Fritzing 0.9.3b)
breadboards: 1

parts:
  U1 = NodeMCU V1.0
  Часть1 = Adafruit BMP180

nets:
  N1: U1.D1, Часть1.SCL
  N2: U1.D2, Часть1.SDA
  GND: U1.GND, Часть1.GND
  VIN: U1.Vin, Часть1.+5V

custom parts:
  NodeMCU V1.0: ESP8266 based NodeMCU
  Adafruit BMP180: This precision sensor from Bosch is the best low-cost sensing solution for measuring barometric pressure and temperature. Because pressure changes with altitude you can also use it as an altimeter! The sensor is soldered onto a PCB with a 3.3V regulator, I2C level shifter and pull-up resistors on the I2C pins. The BMP180 is the next-generation of sensors from Bosch, and replaces the BMP085.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
