# Fritzing sketch Test_water_sensor (saved by Fritzing 0.9.3b)
breadboards: 1

parts:
  U1 = NodeMCU V1.0
  LED1 = LED - 5mm [color="Red (633nm)" package="5 mm [THT]"]
  LED2 = LED - 5mm [color="Yellow (585nm)" package="5 mm [THT]"]
  Water_Level_Sensor = Water Level Sensor

nets:
  N1: U1.D1, LED1.anode
  N2: U1.D2, LED2.anode
  3V3: U1.3V3, Water_Level_Sensor.VCC
  GND: U1.GND, LED1.cathode, LED2.cathode, Water_Level_Sensor.GND
  N3: U1.A0, Water_Level_Sensor.SIG

custom parts:
  NodeMCU V1.0: ESP8266 based NodeMCU
  Water Level Sensor: A water level sensor. This sensor operates at 3V to 5V. The Sig (signal) pin outputs an analogue signal that is in proportion to the amount of water in contact with the sensor.
