# Fritzing sketch 11 (saved by Fritzing 0.9.3b)
breadboards: 3

parts:
  LCD2 = LCD screen
  LCM1602_IIC2 = LCM1602 IIC [part_number="LCM1602 IIC" chip_label="LCM1602 IIC" package="DIP (Dual Inline) [THT]"]
  KY-2 = Keyes Relay [package=THT]
  PIR2 = PIR sensor
  Часть3 = Adafruit BMP180
  U2 = NodeMCU V1.0
  Часть4 = Soil Moisture Sensor
  Q4 = Basic FET N-Channel [package="DPak [SMD]"]
  Q5 = Basic FET N-Channel [package="D2Pak [SMD]"]
  Q6 = Basic FET N-Channel [package="D2Pak [SMD]"]
  R8 = Resistor [tolerance=±5% resistance=100 package=THT]
  R9 = Resistor [tolerance=±5% resistance=100 package=THT]
  R10 = Resistor [tolerance=±5% resistance=100 package=THT]
  Power_plug3 = Power plug
  R11 = Resistor [tolerance=±5% resistance=10k package=THT]
  R12 = Resistor [tolerance=±5% resistance=10k package=THT]
  R13 = Resistor [tolerance=±5% resistance=10k package=THT]
  Power_plug4 = Power plug
  LED4 = LED - 5mm [color="Red (633nm)" package="5 mm [THT]"]
  DS3 = DS18B20 1-Wire Temperature Sensor [part_number=DS18B20]
  DS4 = DS18B20 1-Wire Temperature Sensor [part_number=DS18B20]
  R14 = Resistor [tolerance=±5% resistance=4.7k package=THT]
  LED5 = LED - 5mm [color="Red (633nm)" package="5 mm [THT]"]
  LED6 = LED - 5mm [color="Green (555nm)" package="5 mm [THT]"]

nets:
  VSS: LCD2.VSS, LCM1602_IIC2.VSS
  VDD: LCD2.VDD, LCM1602_IIC2.VDD
  N1: LCD2.V0, LCM1602_IIC2.V0
  N2: LCD2.RS, LCM1602_IIC2.RS
  N3: LCD2.R/W, LCM1602_IIC2.RW
  N4: LCD2.E, LCM1602_IIC2.E
  N5: LCD2.DB0, LCM1602_IIC2.D0
  N6: LCD2.DB1, LCM1602_IIC2.D1
  N7: LCD2.DB2, LCM1602_IIC2.D2
  N8: LCD2.DB3, LCM1602_IIC2.D3
  N9: LCD2.DB4, LCM1602_IIC2.D4
  N10: LCD2.DB5, LCM1602_IIC2.D5
  N11: LCD2.DB6, LCM1602_IIC2.D6
  N12: LCD2.DB7, LCM1602_IIC2.D7
  N13: LCD2.LED+, LCM1602_IIC2.A
  N14: LCD2.LED-, LCM1602_IIC2.K
  GND: LCM1602_IIC2.GND, PIR2.GND, U2.GND, Часть4.GND, Q4.source, Q5.source, Q6.source, Power_plug3.GND, R11.Pin_0, R12.Pin_0, R13.Pin_0, LED4.cathode, DS3.GND, DS4.GND, LED5.cathode, LED6.cathode
  VCC: LCM1602_IIC2.VCC, PIR2.VDD, U2.Vin, Часть4.VCC
  N15: LCM1602_IIC2.SDA, Часть3.SDA, U2.D2
  N16: LCM1602_IIC2.SCL, Часть3.SCL, U2.D1
  N17: LCM1602_IIC2.LED_A, LCM1602_IIC2.LED_B
  N18: KY-2.signal, U2.D0
  +5V: KY-2.power, Часть3.+5V, Power_plug4.VCC
  GND_2: KY-2.ground, Часть3.GND, Power_plug4.GND
  N19: PIR2.SIG, U2.SD3, LED4.anode
  N20: U2.D3, R10.Pin_1
  N21: U2.D4, R9.Pin_1
  VDD_2: U2.3V3, DS3.VDD, DS4.VDD, R14.Pin_0
  N22: U2.D5, R8.Pin_1
  N23: U2.D6, DS3.DQ, DS4.DQ, R14.Pin_1
  N24: U2.D7, LED6.anode
  N25: U2.D8, LED5.anode
  N26: U2.A0, Часть4.SIG
  N27: Q4.Gate, R8.Pin_0, R13.Pin_1
  N28: Q5.Gate, R9.Pin_0, R12.Pin_1
  N29: Q6.Gate, R10.Pin_0, R11.Pin_1

notes:
  светодиодная лента
  12В
  5В

custom parts:
  LCM1602 IIC: I2C-Module to use a 1602 or 2004 LCD on with the wire.h libory Serial LCD Modul
  Keyes Relay: The Keyes 5V relay module is suitable for SCM development, home appliance control. It uses a 5V~12V TIL control signal which can control DC / AC signal.
  Adafruit BMP180: This precision sensor from Bosch is the best low-cost sensing solution for measuring barometric pressure and temperature. Because pressure changes with altitude you can also use it as an altimeter! The sensor is soldered onto a PCB with a 3.3V regulator, I2C level shifter and pull-up resistors on the I2C pins. The BMP180 is the next-generation of sensors from Bosch, and replaces the BMP085.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
  NodeMCU V1.0: ESP8266 based NodeMCU
